// Logisim project CRC.circ as structural Verilog
module CRC (
  input  [7:0] A,
  input  [3:0] B,
  output [10:0] out_3
);

  wire [10:0] bit_extender_1_out, bit_extender_2_out, bit_extender_3_out, bit_extender_4_out,
       bit_extender_5_out, bit_extender_6_out, bit_extender_7_out, bit_extender_8_out, multiplexer_1_out,
       multiplexer_2_out, multiplexer_3_out, multiplexer_4_out, multiplexer_5_out, multiplexer_6_out,
       multiplexer_7_out, multiplexer_8_out, xor_1_out, xor_2_out, xor_3_out, xor_4_out, xor_5_out,
       xor_6_out, xor_7_out;
  wire [10:3] xor_8_out;

  Bit_Extender #(.in_width(11), .out_width(11)) bit_extender_1 (.in({B, {7{1'b0}}}), .out(bit_extender_1_out));
  assign bit_extender_2_out = {{1{1'b0}}, {B, {6{1'b0}}}};  // Bit_Extender bit_extender_2
  assign bit_extender_3_out = {{2{1'b0}}, {B, {5{1'b0}}}};  // Bit_Extender bit_extender_3
  assign bit_extender_4_out = {{3{1'b0}}, {B, 4'b0000}};  // Bit_Extender bit_extender_4
  assign bit_extender_5_out = {{4{1'b0}}, {B, 3'b000}};  // Bit_Extender bit_extender_5
  assign bit_extender_6_out = {{5{1'b0}}, {B, 2'b00}};  // Bit_Extender bit_extender_6
  assign bit_extender_7_out = {{6{1'b0}}, {B, 1'b0}};  // Bit_Extender bit_extender_7
  assign bit_extender_8_out = {{7{1'b0}}, B};  // Bit_Extender bit_extender_8
  Multiplexer #(.width(11), .disabled(0)) multiplexer_1 (
    .in0({11{1'b0}}), .in1(bit_extender_1_out), .out(multiplexer_1_out), .sel(A[7]));  // open: en
  Multiplexer #(.width(11), .disabled(0)) multiplexer_2 (
    .in0({11{1'b0}}), .in1(bit_extender_2_out), .out(multiplexer_2_out), .sel(xor_1_out[9]));  // open: en
  Multiplexer #(.width(11), .disabled(0)) multiplexer_3 (
    .in0({11{1'b0}}), .in1(bit_extender_3_out), .out(multiplexer_3_out), .sel(xor_2_out[8]));  // open: en
  Multiplexer #(.width(11), .disabled(0)) multiplexer_4 (
    .in0({11{1'b0}}), .in1(bit_extender_4_out), .out(multiplexer_4_out), .sel(xor_3_out[7]));  // open: en
  Multiplexer #(.width(11), .disabled(0)) multiplexer_5 (
    .in0({11{1'b0}}), .in1(bit_extender_5_out), .out(multiplexer_5_out), .sel(xor_4_out[6]));  // open: en
  Multiplexer #(.width(11), .disabled(0)) multiplexer_6 (
    .in0({11{1'b0}}), .in1(bit_extender_6_out), .out(multiplexer_6_out), .sel(xor_5_out[5]));  // open: en
  Multiplexer #(.width(11), .disabled(0)) multiplexer_7 (
    .in0({11{1'b0}}), .in1(bit_extender_7_out), .out(multiplexer_7_out), .sel(xor_6_out[4]));  // open: en
  Multiplexer #(.width(11), .disabled(0)) multiplexer_8 (
    .in0({11{1'b0}}), .in1(bit_extender_8_out), .out(multiplexer_8_out), .sel(xor_7_out[3]));  // open: en
  assign xor_1_out = {A, 3'b000} ^ multiplexer_1_out;  // XOR_Gate xor_1, 11 bits wide
  assign xor_2_out = xor_1_out ^ multiplexer_2_out;  // XOR_Gate xor_2, 11 bits wide
  assign xor_3_out = xor_2_out ^ multiplexer_3_out;  // XOR_Gate xor_3, 11 bits wide
  assign xor_4_out = xor_3_out ^ multiplexer_4_out;  // XOR_Gate xor_4, 11 bits wide
  assign xor_5_out = xor_4_out ^ multiplexer_5_out;  // XOR_Gate xor_5, 11 bits wide
  assign xor_6_out = xor_5_out ^ multiplexer_6_out;  // XOR_Gate xor_6, 11 bits wide
  assign xor_7_out = xor_6_out ^ multiplexer_7_out;  // XOR_Gate xor_7, 11 bits wide
  assign {xor_8_out, out_3[2:0]} = xor_7_out ^ multiplexer_8_out;  // XOR_Gate xor_8, 11 bits wide

  assign out_3[10:3] = A;
endmodule
