// Logisim project fibonacci_1.circ as structural Verilog: 1 circuit, main circuit main
module main (
  input  [2:0] N,
  output [3:0] Out
);

  wire clock_1_out, comparator_1_gt, comparator_1_lt, Init_q;
  wire [3:0] adder_1_out, F_n_1_q, F_n_q, multiplexer_1_out;
  wire [7:0] bit_extender_1_out, counter_1_q;

  Clock clock_1 (.out(clock_1_out));
  assign bit_extender_1_out = {{5{1'b0}}, N};  // Bit_Extender bit_extender_1
  Counter counter_1 (.count(1'b1), .Q(counter_1_q), .clk(clock_1_out));  // open: load, D, carry, clr
  Register #(.width(1)) Init (.D(1'b1), .en(1'b1), .Q(Init_q), .clk(clock_1_out));  // open: clr
  Comparator #(.mode("unsigned")) comparator_1 (
    .a(bit_extender_1_out), .b(counter_1_q), .gt(comparator_1_gt), .lt(comparator_1_lt));  // open: eq
  Multiplexer #(.width(4)) multiplexer_1 (
    .in0(4'b0001), .in1(adder_1_out), .out(multiplexer_1_out), .sel(Init_q));  // open: en
  Register #(.width(4)) F_n (.D(F_n_1_q), .en(comparator_1_gt), .Q(F_n_q), .clk(clock_1_out));  // open: clr
  Register #(.width(4)) F_n_1 (
    .D(multiplexer_1_out), .en(comparator_1_gt), .Q(F_n_1_q), .clk(clock_1_out));  // open: clr
  Adder #(.width(4)) adder_1 (.a(F_n_q), .b(F_n_1_q), .out(adder_1_out));  // open: cin, cout
  Multiplexer #(.width(4)) multiplexer_2 (.in0(4'b0000), .in1(F_n_1_q), .out(Out), .sel(comparator_1_lt));  // open: en
endmodule
