// Logisim project fibonacci_2.circ as structural Verilog: 3 circuits, main circuit main
module main (
  input  [31:0] N,
  output [31:0] out_2
);

  wire clock_1_out, comparator_1_eq, Inited_q;
  wire [31:0] B00_q, B01_q, B10_q, B11_q, B_prime_00, B_prime_01, B_prime_10, B_prime_11, multiplexer_1_out,
       mux4_1_o0, mux4_1_o1, mux4_1_o2, mux4_1_o3, mux4_2_o0, mux4_2_o1, mux4_2_o2, mux4_2_o3, N_q, R00,
       R00_q, R01, R01_q, R10, R10_q, R11, R11_q, R_prime_00, R_prime_01, R_prime_10, R_prime_11,
       shifter_1_out;

  Clock clock_1 (.out(clock_1_out));
  Register #(.width(1)) Inited (.D(1'b1), .en(1'b1), .Q(Inited_q), .clk(clock_1_out));  // open: clr
  Multiplexer #(.width(32)) multiplexer_1 (
    .in0(N), .in1(shifter_1_out), .out(multiplexer_1_out), .sel(Inited_q));  // open: en
  Shifter #(.width(32), .shift("lr")) shifter_1 (.in(N_q), .\dist (5'b00001), .out(shifter_1_out));
  Comparator #(.width(32), .mode("unsigned")) comparator_1 (
    .a({32{1'b0}}), .b(N_q), .eq(comparator_1_eq));  // open: gt, lt
  Register #(.width(32)) u_N (.D(multiplexer_1_out), .en(1'b1), .Q(N_q), .clk(clock_1_out));  // open: clr
  mux4 mux4_1 (
    .a0(32'h1), .a1(32'h1), .a2(32'h1), .a3({32{1'b0}}), .b0(B_prime_00), .b1(B_prime_01), .b2(B_prime_10),
    .b3(B_prime_11), .Control(Inited_q), .o0(mux4_1_o0), .o1(mux4_1_o1), .o2(mux4_1_o2), .o3(mux4_1_o3));
  mux4 mux4_2 (
    .a0(R00), .a1(R01), .a2(R10), .a3(R11), .b0(R_prime_00), .b1(R_prime_01), .b2(R_prime_10),
    .b3(R_prime_11), .Control(N_q[0]), .o0(mux4_2_o0), .o1(mux4_2_o1), .o2(mux4_2_o2), .o3(mux4_2_o3));
  Register #(.width(32)) B00 (.D(mux4_1_o0), .en(1'b1), .Q(B00_q), .clk(clock_1_out));  // open: clr
  Register #(.width(32)) B01 (.D(mux4_1_o1), .en(1'b1), .Q(B01_q), .clk(clock_1_out));  // open: clr
  Register #(.width(32)) B10 (.D(mux4_1_o2), .en(1'b1), .Q(B10_q), .clk(clock_1_out));  // open: clr
  Register #(.width(32)) B11 (.D(mux4_1_o3), .en(1'b1), .Q(B11_q), .clk(clock_1_out));  // open: clr
  Register #(.width(32)) u_R00 (.D(mux4_2_o0), .en(1'b1), .Q(R00_q), .clk(clock_1_out));  // open: clr
  Register #(.width(32)) u_R01 (.D(mux4_2_o1), .en(1'b1), .Q(R01_q), .clk(clock_1_out));  // open: clr
  Register #(.width(32)) u_R10 (.D(mux4_2_o2), .en(1'b1), .Q(R10_q), .clk(clock_1_out));  // open: clr
  Register #(.width(32)) u_R11 (.D(mux4_2_o3), .en(1'b1), .Q(R11_q), .clk(clock_1_out));  // open: clr
  matmul matmul_1 (
    .a00(B00_q), .a01(B01_q), .a10(B10_q), .a11(B11_q), .b00(B00_q), .b01(B01_q), .b10(B10_q), .b11(B11_q),
    .c00(B_prime_00), .c01(B_prime_01), .c10(B_prime_10), .c11(B_prime_11));
  matmul matmul_2 (
    .a00(R00_q), .a01(R01_q), .a10(R10_q), .a11(R11_q), .b00(B00_q), .b01(B01_q), .b10(B10_q), .b11(B11_q),
    .c00(R_prime_00), .c01(R_prime_01), .c10(R_prime_10), .c11(R_prime_11));
  mux4 mux4_3 (
    .a0(32'h1), .a1({32{1'b0}}), .a2({32{1'b0}}), .a3(32'h1), .b0(R00_q), .b1(R01_q), .b2(R10_q), .b3(R11_q),
    .Control(Inited_q), .o0(R00), .o1(R01), .o2(R10), .o3(R11));
  Multiplexer #(.width(32)) multiplexer_2 (
    .in0({32{1'b0}}), .in1(R10), .out(out_2), .sel(comparator_1_eq));  // open: en
endmodule

module matmul (
  input  [31:0] a00,
  input  [31:0] a01,
  input  [31:0] a10,
  input  [31:0] a11,
  input  [31:0] b00,
  input  [31:0] b01,
  input  [31:0] b10,
  input  [31:0] b11,
  output [31:0] c00,
  output [31:0] c01,
  output [31:0] c10,
  output [31:0] c11
);

  wire [31:0] multiplier_1_out, multiplier_2_out, multiplier_3_out, multiplier_4_out, multiplier_5_out,
       multiplier_6_out, multiplier_7_out, multiplier_8_out;

  Multiplier #(.width(32)) multiplier_1 (.a(a00), .b(b00), .out(multiplier_1_out));  // open: cin, cout
  Multiplier #(.width(32)) multiplier_2 (.a(a01), .b(b10), .out(multiplier_2_out));  // open: cin, cout
  Multiplier #(.width(32)) multiplier_3 (.a(a00), .b(b01), .out(multiplier_3_out));  // open: cin, cout
  Multiplier #(.width(32)) multiplier_4 (.a(a01), .b(b11), .out(multiplier_4_out));  // open: cin, cout
  Multiplier #(.width(32)) multiplier_5 (.a(a10), .b(b00), .out(multiplier_5_out));  // open: cin, cout
  Multiplier #(.width(32)) multiplier_6 (.a(a11), .b(b10), .out(multiplier_6_out));  // open: cin, cout
  Multiplier #(.width(32)) multiplier_7 (.a(a10), .b(b01), .out(multiplier_7_out));  // open: cin, cout
  Multiplier #(.width(32)) multiplier_8 (.a(a11), .b(b11), .out(multiplier_8_out));  // open: cin, cout
  Adder #(.width(32)) adder_1 (.a(multiplier_1_out), .b(multiplier_2_out), .out(c00));  // open: cin, cout
  Adder #(.width(32)) adder_2 (.a(multiplier_3_out), .b(multiplier_4_out), .out(c01));  // open: cin, cout
  Adder #(.width(32)) adder_3 (.a(multiplier_5_out), .b(multiplier_6_out), .out(c10));  // open: cin, cout
  Adder #(.width(32)) adder_4 (.a(multiplier_7_out), .b(multiplier_8_out), .out(c11));  // open: cin, cout
endmodule

module mux4 (
  input  [31:0] a0,
  input  [31:0] a1,
  input  [31:0] a2,
  input  [31:0] a3,
  input  [31:0] b0,
  input  [31:0] b1,
  input  [31:0] b2,
  input  [31:0] b3,
  input  Control,
  output [31:0] o0,
  output [31:0] o1,
  output [31:0] o2,
  output [31:0] o3
);

  Multiplexer #(.width(32)) multiplexer_1 (.in0(a0), .in1(b0), .out(o0), .sel(Control));  // open: en
  Multiplexer #(.width(32)) multiplexer_2 (.in0(a1), .in1(b1), .out(o1), .sel(Control));  // open: en
  Multiplexer #(.width(32)) multiplexer_3 (.in0(a2), .in1(b2), .out(o2), .sel(Control));  // open: en
  Multiplexer #(.width(32)) multiplexer_4 (.in0(a3), .in1(b3), .out(o3), .sel(Control));  // open: en
endmodule
