// Logisim project fsm.circ as structural Verilog
module fsm (
  input  [1:0] in,
  input  clr,
  output z
);

  wire clock_1_out;
  wire [1:0] fsm_internal_1_t, multiplexer_1_out, state_q;

  Clock clock_1 (.out(clock_1_out));
  Multiplexer #(.width(2), .enable("false")) multiplexer_1 (
    .in0(fsm_internal_1_t), .in1(2'b00), .out(multiplexer_1_out), .sel(clr));
  Register #(.width(2)) state (.D(multiplexer_1_out), .Q(state_q), .clk(clock_1_out));  // open: en, clr
  fsm_internal fsm_internal_1 (.s(state_q), .in(in), .t(fsm_internal_1_t));
  Comparator #(.width(2)) comparator_1 (.a(fsm_internal_1_t), .b(2'b11), .eq(z));  // open: gt, lt
endmodule

module fsm_internal (
  input  [1:0] s,
  input  [1:0] in,
  output [1:0] t
);

  wire and_1_out, and_2_out, and_3_out, and_4_out, not_1_out, not_2_out, not_3_out, not_4_out, not_5_out,
       not_6_out, not_7_out;

  not not_1 (not_1_out, s[1]);
  not not_2 (not_2_out, in[0]);
  not not_3 (not_3_out, s[0]);
  not not_4 (not_4_out, in[0]);
  not not_5 (not_5_out, in[1]);
  not not_6 (not_6_out, s[0]);
  not not_7 (not_7_out, in[0]);
  and and_1 (and_1_out, not_1_out, s[0], not_2_out);
  and and_2 (and_2_out, s[1], not_3_out, not_4_out);
  and and_3 (and_3_out, not_5_out, in[0]);
  and and_4 (and_4_out, s[1], not_6_out, not_7_out);
  or or_1 (t[1], and_1_out, and_2_out);
  or or_2 (t[0], and_3_out, and_4_out);
endmodule
