// Logisim project ftoi.circ as structural Verilog
module ftoi (
  input  [15:0] in_1,
  output [31:0] out_2
);

  wire comparator_1_eq, comparator_2_lt, comparator_3_eq;
  wire [4:0] subtractor_1_out, subtractor_2_out;
  wire [10:10] not_1_out;
  wire [31:0] bit_extender_1_out, multiplexer_1_out, multiplexer_2_out, negator_1_out, shifter_1_out,
       shifter_2_out;

  Comparator #(.width(5)) comparator_1 (.a({5{1'b0}}), .b(in_1[14:10]), .eq(comparator_1_eq));  // open: gt, lt
  not not_1 (not_1_out[10], comparator_1_eq);
  Comparator #(.width(5), .mode("unsigned")) comparator_2 (
    .a(in_1[14:10]), .b(5'b11001), .lt(comparator_2_lt));  // open: gt, eq
  assign bit_extender_1_out = {{21{1'b0}}, {not_1_out[10], in_1[9:0]}};  // Bit_Extender bit_extender_1
  Subtractor #(.width(5)) subtractor_1 (.a(in_1[14:10]), .b(5'b11001), .out(subtractor_1_out));  // open: bin, bout
  Subtractor #(.width(5)) subtractor_2 (.a(5'b11001), .b(in_1[14:10]), .out(subtractor_2_out));  // open: bin, bout
  Shifter #(.width(32)) shifter_1 (.in(bit_extender_1_out), .\dist (subtractor_1_out), .out(shifter_1_out));
  Shifter #(.width(32), .shift("lr")) shifter_2 (
    .in(bit_extender_1_out), .\dist (subtractor_2_out), .out(shifter_2_out));
  Multiplexer #(.width(32), .disabled(0), .enable("false")) multiplexer_1 (
    .in0(shifter_1_out), .in1(shifter_2_out), .out(multiplexer_1_out), .sel(comparator_2_lt));
  Comparator #(.width(5)) comparator_3 (.a(in_1[14:10]), .b({5{1'b1}}), .eq(comparator_3_eq));  // open: gt, lt
  Negator #(.width(32)) negator_1 (.in(multiplexer_1_out), .out(negator_1_out));
  Multiplexer #(.width(32), .disabled(0), .enable("false")) multiplexer_2 (
    .in0(multiplexer_1_out), .in1(negator_1_out), .out(multiplexer_2_out), .sel(in_1[15]));
  Multiplexer #(.width(32), .disabled(0), .enable("false")) multiplexer_3 (
    .in0(multiplexer_2_out), .in1({32{1'b0}}), .out(out_2), .sel(comparator_3_eq));
endmodule
