// Logisim project grf.circ as structural Verilog
module grf (
  input  clk,
  input  reset,
  input  we,
  input  [4:0] A1,
  input  [4:0] A2,
  input  [4:0] A3,
  input  [31:0] wd,
  output [31:0] rd1,
  output [31:0] rd2
);

  wire comparator_1_eq, comparator_2_eq;
  wire [31:0] grf_base5_1_rd1, grf_base5_1_rd2;

  grf_base5 grf_base5_1 (
    .A1(A1), .A2(A2), .A3(A3), .wd(wd), .rd1(grf_base5_1_rd1), .rd2(grf_base5_1_rd2), .clk(clk),
    .reset(reset), .we(we));
  Comparator #(.width(5)) comparator_1 (.a(A1), .b({5{1'b0}}), .eq(comparator_1_eq));  // open: gt, lt
  Multiplexer #(.width(32), .disabled(0), .enable("false")) multiplexer_1 (
    .in0(grf_base5_1_rd1), .in1({32{1'b0}}), .out(rd1), .sel(comparator_1_eq));
  Comparator #(.width(5)) comparator_2 (.a(A2), .b({5{1'b0}}), .eq(comparator_2_eq));  // open: gt, lt
  Multiplexer #(.width(32), .disabled(0), .enable("false")) multiplexer_2 (
    .in0(grf_base5_1_rd2), .in1({32{1'b0}}), .out(rd2), .sel(comparator_2_eq));
endmodule

module grf_base1 (
  input  clk,
  input  reset,
  input  we,
  input  A1,
  input  A2,
  input  A3,
  input  [31:0] wd,
  output [31:0] rd1,
  output [31:0] rd2
);

  wire demultiplexer_1_out0, demultiplexer_1_out1;
  wire [31:0] register_1_q, register_2_q;

  Demultiplexer #(.disabled(0), .enable("false")) demultiplexer_1 (
    .out0(demultiplexer_1_out0), .out1(demultiplexer_1_out1), .in(we), .sel(A3));
  Register #(.width(32)) register_1 (.D(wd), .en(demultiplexer_1_out0), .Q(register_1_q), .clk(clk), .clr(reset));
  Register #(.width(32)) register_2 (.D(wd), .en(demultiplexer_1_out1), .Q(register_2_q), .clk(clk), .clr(reset));
  Multiplexer #(.width(32), .enable("false")) multiplexer_1 (
    .in0(register_1_q), .in1(register_2_q), .out(rd1), .sel(A1));
  Multiplexer #(.width(32), .enable("false")) multiplexer_2 (
    .in0(register_1_q), .in1(register_2_q), .out(rd2), .sel(A2));
endmodule

module grf_base2 (
  input  clk,
  input  reset,
  input  we,
  input  [1:0] A1,
  input  [1:0] A2,
  input  [1:0] A3,
  input  [31:0] wd,
  output [31:0] rd1,
  output [31:0] rd2
);

  wire demultiplexer_1_out0, demultiplexer_1_out1;
  wire [31:0] grf_base1_1_rd1, grf_base1_1_rd2, grf_base1_2_rd1, grf_base1_2_rd2;

  grf_base1 grf_base1_1 (
    .A1(A1[0]), .A2(A2[0]), .A3(A3[0]), .wd(wd), .rd1(grf_base1_1_rd1), .rd2(grf_base1_1_rd2), .clk(clk),
    .reset(reset), .we(demultiplexer_1_out0));
  grf_base1 grf_base1_2 (
    .A1(A1[0]), .A2(A2[0]), .A3(A3[0]), .wd(wd), .rd1(grf_base1_2_rd1), .rd2(grf_base1_2_rd2), .clk(clk),
    .reset(reset), .we(demultiplexer_1_out1));
  Demultiplexer #(.enable("false")) demultiplexer_1 (
    .out0(demultiplexer_1_out0), .out1(demultiplexer_1_out1), .in(we), .sel(A3[1]));
  Multiplexer #(.width(32), .enable("false")) multiplexer_1 (
    .in0(grf_base1_1_rd1), .in1(grf_base1_2_rd1), .out(rd1), .sel(A1[1]));
  Multiplexer #(.width(32), .enable("false")) multiplexer_2 (
    .in0(grf_base1_1_rd2), .in1(grf_base1_2_rd2), .out(rd2), .sel(A2[1]));
endmodule

module grf_base3 (
  input  clk,
  input  reset,
  input  we,
  input  [2:0] A1,
  input  [2:0] A2,
  input  [2:0] A3,
  input  [31:0] wd,
  output [31:0] rd1,
  output [31:0] rd2
);

  wire demultiplexer_1_out0, demultiplexer_1_out1;
  wire [31:0] grf_base2_1_rd1, grf_base2_1_rd2, grf_base2_2_rd1, grf_base2_2_rd2;

  grf_base2 grf_base2_1 (
    .A1(A1[1:0]), .A2(A2[1:0]), .A3(A3[1:0]), .wd(wd), .rd1(grf_base2_1_rd1), .rd2(grf_base2_1_rd2),
    .clk(clk), .reset(reset), .we(demultiplexer_1_out0));
  grf_base2 grf_base2_2 (
    .A1(A1[1:0]), .A2(A2[1:0]), .A3(A3[1:0]), .wd(wd), .rd1(grf_base2_2_rd1), .rd2(grf_base2_2_rd2),
    .clk(clk), .reset(reset), .we(demultiplexer_1_out1));
  Demultiplexer #(.enable("false")) demultiplexer_1 (
    .out0(demultiplexer_1_out0), .out1(demultiplexer_1_out1), .in(we), .sel(A3[2]));
  Multiplexer #(.width(32), .enable("false")) multiplexer_1 (
    .in0(grf_base2_1_rd1), .in1(grf_base2_2_rd1), .out(rd1), .sel(A1[2]));
  Multiplexer #(.width(32), .enable("false")) multiplexer_2 (
    .in0(grf_base2_1_rd2), .in1(grf_base2_2_rd2), .out(rd2), .sel(A2[2]));
endmodule

module grf_base4 (
  input  clk,
  input  reset,
  input  we,
  input  [3:0] A1,
  input  [3:0] A2,
  input  [3:0] A3,
  input  [31:0] wd,
  output [31:0] rd1,
  output [31:0] rd2
);

  wire demultiplexer_1_out0, demultiplexer_1_out1;
  wire [31:0] grf_base3_1_rd1, grf_base3_1_rd2, grf_base3_2_rd1, grf_base3_2_rd2;

  grf_base3 grf_base3_1 (
    .A1(A1[2:0]), .A2(A2[2:0]), .A3(A3[2:0]), .wd(wd), .rd1(grf_base3_1_rd1), .rd2(grf_base3_1_rd2),
    .clk(clk), .reset(reset), .we(demultiplexer_1_out0));
  grf_base3 grf_base3_2 (
    .A1(A1[2:0]), .A2(A2[2:0]), .A3(A3[2:0]), .wd(wd), .rd1(grf_base3_2_rd1), .rd2(grf_base3_2_rd2),
    .clk(clk), .reset(reset), .we(demultiplexer_1_out1));
  Demultiplexer #(.enable("false")) demultiplexer_1 (
    .out0(demultiplexer_1_out0), .out1(demultiplexer_1_out1), .in(we), .sel(A3[3]));
  Multiplexer #(.width(32), .enable("false")) multiplexer_1 (
    .in0(grf_base3_1_rd1), .in1(grf_base3_2_rd1), .out(rd1), .sel(A1[3]));
  Multiplexer #(.width(32), .enable("false")) multiplexer_2 (
    .in0(grf_base3_1_rd2), .in1(grf_base3_2_rd2), .out(rd2), .sel(A2[3]));
endmodule

module grf_base5 (
  input  clk,
  input  reset,
  input  we,
  input  [4:0] A1,
  input  [4:0] A2,
  input  [4:0] A3,
  input  [31:0] wd,
  output [31:0] rd1,
  output [31:0] rd2
);

  wire demultiplexer_1_out0, demultiplexer_1_out1;
  wire [31:0] grf_base4_1_rd1, grf_base4_1_rd2, grf_base4_2_rd1, grf_base4_2_rd2;

  grf_base4 grf_base4_1 (
    .A1(A1[3:0]), .A2(A2[3:0]), .A3(A3[3:0]), .wd(wd), .rd1(grf_base4_1_rd1), .rd2(grf_base4_1_rd2),
    .clk(clk), .reset(reset), .we(demultiplexer_1_out0));
  grf_base4 grf_base4_2 (
    .A1(A1[3:0]), .A2(A2[3:0]), .A3(A3[3:0]), .wd(wd), .rd1(grf_base4_2_rd1), .rd2(grf_base4_2_rd2),
    .clk(clk), .reset(reset), .we(demultiplexer_1_out1));
  Demultiplexer #(.enable("false")) demultiplexer_1 (
    .out0(demultiplexer_1_out0), .out1(demultiplexer_1_out1), .in(we), .sel(A3[4]));
  Multiplexer #(.width(32), .enable("false")) multiplexer_1 (
    .in0(grf_base4_1_rd1), .in1(grf_base4_2_rd1), .out(rd1), .sel(A1[4]));
  Multiplexer #(.width(32), .enable("false")) multiplexer_2 (
    .in0(grf_base4_1_rd2), .in1(grf_base4_2_rd2), .out(rd2), .sel(A2[4]));
endmodule
