// Logisim project navigation.circ as structural Verilog
module navigation (
  input  [1:0] dir,
  input  clk,
  input  reset,
  output arrive,
  output hit
);

  wire comparator_1_eq, comparator_2_eq, not_1_out;
  wire [3:0] rom_1_data;
  wire [5:2] pos_q;

  Register #(.width(4)) pos (.D(rom_1_data), .en(not_1_out), .Q(pos_q), .clk(clk), .clr(reset));
  ROM #(.addrWidth(6), .dataWidth(4)) rom_1 (.addr({pos_q, dir}), .data(rom_1_data));  // open: sel
  Comparator #(.width(4)) comparator_1 (.a(rom_1_data), .b(4'b0100), .eq(comparator_1_eq));  // open: gt, lt
  Comparator #(.width(4)) comparator_2 (.a(rom_1_data), .b(4'b1111), .eq(comparator_2_eq));  // open: gt, lt
  D_Flip_Flop d_ff_1 (.clk(clk), .D(comparator_1_eq), .Q(arrive), .reset(reset));  // open: Qn, preset, en
  D_Flip_Flop d_ff_2 (.clk(clk), .D(comparator_2_eq), .Q(hit), .reset(reset));  // open: Qn, preset, en
  not not_1 (not_1_out, comparator_2_eq);

  // Notes on the sheet:
  //   contents of rom_1 (hex, n*v repeats v):
  //   1 f f f 3 2 0 f 4 f f 1 f 4 1 f
endmodule
