// Logisim project power_mod_5.circ as structural Verilog
module mod5 (
  input  In,
  output s0_prime,
  output s1_prime,
  output s2_prime,
  output s3_prime,
  output s4_prime
);

  wire clock_1_out;
  wire [2:0] register_1_q, transition_1_t0;

  Clock clock_1 (.out(clock_1_out));
  Register #(.width(3)) register_1 (.D(transition_1_t0), .en(1'b1), .Q(register_1_q), .clk(clock_1_out));  // open: clr
  Decoder #(.select(3)) decoder_1 (
    .out0(s0_prime), .out1(s1_prime), .out2(s2_prime), .out3(s3_prime), .out4(s4_prime),
    .sel(transition_1_t0), .en(1'b1));  // open: out5, out6, out7
  transition transition_1 (
    .in(In), .s0(register_1_q[0]), .s1(register_1_q[1]), .s2(register_1_q[2]), .t0(transition_1_t0[0]),
    .t1(transition_1_t0[1]), .t2(transition_1_t0[2]));
endmodule

module transition (
  input  in,
  input  s0,
  input  s1,
  input  s2,
  output t0,
  output t1,
  output t2
);

  wire and_1_out, and_2_out, not_1_out, not_2_out, not_3_out;

  not not_1 (not_1_out, in);
  and and_1 (and_1_out, not_1_out, not_2_out);
  not not_2 (not_2_out, s1);
  and and_2 (and_2_out, in, s1);
  not not_3 (not_3_out, in);
  and and_3 (t2, not_3_out, s1);
  or or_1 (t0, and_1_out, and_2_out);

  assign t1 = in;
endmodule
