// Logisim project single_cycle_cpu.circ as structural Verilog: 6 circuits, main circuit main
module main (
  input  reset,
  output [31:0] out_2,
  output [31:0] out_3,
  output out_4,
  output [4:0] out_5,
  output [31:0] out_6,
  output out_7,
  output [31:0] out_8,
  output [31:0] out_9
);

  wire clk_out, ctrl_1_pcstore;
  wire [4:0] dec_1_rd, dec_1_rs, dec_1_rt, dec_1_shamt;
  wire [5:0] dec_1_funct, dec_1_opcode;
  wire [15:0] dec_1_imm;
  wire [25:0] dec_1_jmm;
  wire [31:0] ctrl_1_pcstoredata, dm_1_memdata, grf_1_rdata1, grf_1_rdata2;

  Clock clk (.out(clk_out));
  IFU ifu_1 (.we(ctrl_1_pcstore), .wd(ctrl_1_pcstoredata), .clk(clk_out), .clr(reset), .pc(out_3), .instr(out_2));
  DEC dec_1 (
    .instr(out_2), .opcode(dec_1_opcode), .rs(dec_1_rs), .rt(dec_1_rt), .rd(dec_1_rd), .shamt(dec_1_shamt),
    .funct(dec_1_funct), .imm(dec_1_imm), .jmm(dec_1_jmm));
  DM dm_1 (.memStore(out_7), .memAddr(out_8), .memStoreData(out_9), .clk(clk_out), .clr(reset), .memData(dm_1_memdata));
  GRF grf_1 (
    .rs(dec_1_rs), .rd(out_5), .we(out_4), .rt(dec_1_rt), .clk(clk_out), .wd(out_6), .clr(reset),
    .rdata1(grf_1_rdata1), .rdata2(grf_1_rdata2));
  CTRL ctrl_1 (
    .opcode(dec_1_opcode), .rs(dec_1_rs), .rt(dec_1_rt), .rd(dec_1_rd), .shamt(dec_1_shamt),
    .funct(dec_1_funct), .imm(dec_1_imm), .jmm(dec_1_jmm), .rs_2(grf_1_rdata1), .rt_2(grf_1_rdata2),
    .memData(dm_1_memdata), .memStore(out_7), .memAddr(out_8), .memStoreData(out_9), .regStore(out_4),
    .regStoreData(out_6), .regAddr(out_5), .pcStore(ctrl_1_pcstore), .pcStoreData(ctrl_1_pcstoredata),
    .pc(out_3));

  // Other names for the same wires on the sheet: instr[31:0] = out_2; memAddr[31:0] = out_8; memStore = out_7;
  //   memStoreData[31:0] = out_9; pc[31:0] = out_3; regAddr[4:0] = out_5; regData[31:0] = out_6; regStore = out_4
endmodule

module IFU (
  input  we,
  input  [31:0] wd,
  input  clk,
  input  clr,
  output [31:0] pc,
  output [31:0] instr
);

  wire [31:0] adder_1_out, multiplexer_1_out, pc_q, subtractor_1_out;

  Adder #(.width(32)) adder_1 (.a(pc_q), .b(32'h4), .out(adder_1_out));  // open: cin, cout
  Multiplexer #(.width(32), .enable("false")) multiplexer_1 (
    .in0(adder_1_out), .in1(subtractor_1_out), .out(multiplexer_1_out), .sel(we));
  Subtractor #(.width(32)) subtractor_1 (.a(wd), .b(32'h3000), .out(subtractor_1_out));  // open: bin, bout
  Register #(.width(32)) u_pc (.D(multiplexer_1_out), .Q(pc_q), .clk(clk), .clr(clr));  // open: en
  Adder #(.width(32)) adder_2 (.a(pc_q), .b(32'h3000), .out(pc));  // open: cin, cout
  ROM #(.addrWidth(12), .dataWidth(32)) rom_1 (.addr(pc_q[13:2]), .data(instr));  // open: sel
endmodule

module DEC (
  input  [31:0] instr,
  output [5:0] opcode,
  output [4:0] rs,
  output [4:0] rt,
  output [4:0] rd,
  output [4:0] shamt,
  output [5:0] funct,
  output [15:0] imm,
  output [25:0] jmm
);


  assign funct = instr[5:0];
  assign imm = instr[15:0];
  assign jmm = instr[25:0];
  assign opcode = instr[31:26];
  assign rd = instr[15:11];
  assign rs = instr[25:21];
  assign rt = instr[20:16];
  assign shamt = instr[10:6];
endmodule

module GRF (
  input  clk,
  input  clr,
  input  we,
  input  [4:0] rs,
  input  [4:0] rt,
  input  [4:0] rd,
  input  [31:0] wd,
  output [31:0] rdata1,
  output [31:0] rdata2
);

  wire EN01, EN02, EN03, EN04, EN05, EN06, EN07, EN08, EN09, EN10, EN11, EN12, EN13, EN14, EN15, EN16, EN17,
       EN18, EN19, EN20, EN21, EN22, EN23, EN24, EN25, EN26, EN27, EN28, EN29, EN30, EN31;
  wire [31:0] R01, R02, R03, R04, R05, R06, R07, R08, R09, R10, R11, R12, R13, R14, R15, R16, R17, R18, R19,
       R20, R21, R22, R23, R24, R25, R26, R27, R28, R29, R30, R31;

  Register #(.width(32)) _01 (.D(wd), .en(EN01), .Q(R01), .clk(clk), .clr(clr));
  Register #(.width(32)) _02 (.D(wd), .en(EN02), .Q(R02), .clk(clk), .clr(clr));
  Register #(.width(32)) _03 (.D(wd), .en(EN03), .Q(R03), .clk(clk), .clr(clr));
  Register #(.width(32)) _04 (.D(wd), .en(EN04), .Q(R04), .clk(clk), .clr(clr));
  Register #(.width(32)) _05 (.D(wd), .en(EN05), .Q(R05), .clk(clk), .clr(clr));
  Register #(.width(32)) _06 (.D(wd), .en(EN06), .Q(R06), .clk(clk), .clr(clr));
  Register #(.width(32)) _07 (.D(wd), .en(EN07), .Q(R07), .clk(clk), .clr(clr));
  Register #(.width(32)) _08 (.D(wd), .en(EN08), .Q(R08), .clk(clk), .clr(clr));
  Decoder #(.select(5), .disabled(0)) decoder_1 (
    .out1(EN01), .out2(EN02), .out3(EN03), .out4(EN04), .out5(EN05), .out6(EN06), .out7(EN07), .out8(EN08),
    .out9(EN09), .out10(EN10), .out11(EN11), .out12(EN12), .out13(EN13), .out14(EN14), .out15(EN15),
    .out16(EN16), .out17(EN17), .out18(EN18), .out19(EN19), .out20(EN20), .out21(EN21), .out22(EN22),
    .out23(EN23), .out24(EN24), .out25(EN25), .out26(EN26), .out27(EN27), .out28(EN28), .out29(EN29),
    .out30(EN30), .out31(EN31), .sel(rd), .en(we));  // open: out0
  Register #(.width(32)) _09 (.D(wd), .en(EN09), .Q(R09), .clk(clk), .clr(clr));
  Register #(.width(32)) _10 (.D(wd), .en(EN10), .Q(R10), .clk(clk), .clr(clr));
  Register #(.width(32)) _11 (.D(wd), .en(EN11), .Q(R11), .clk(clk), .clr(clr));
  Register #(.width(32)) _12 (.D(wd), .en(EN12), .Q(R12), .clk(clk), .clr(clr));
  Register #(.width(32)) _13 (.D(wd), .en(EN13), .Q(R13), .clk(clk), .clr(clr));
  Register #(.width(32)) _14 (.D(wd), .en(EN14), .Q(R14), .clk(clk), .clr(clr));
  Register #(.width(32)) _15 (.D(wd), .en(EN15), .Q(R15), .clk(clk), .clr(clr));
  Register #(.width(32)) _16 (.D(wd), .en(EN16), .Q(R16), .clk(clk), .clr(clr));
  Multiplexer #(.select(5), .width(32), .disabled(0), .enable("false")) multiplexer_1 (
    .in0({32{1'b0}}), .in1(R01), .in2(R02), .in3(R03), .in4(R04), .in5(R05), .in6(R06), .in7(R07), .in8(R08),
    .in9(R09), .in10(R10), .in11(R11), .in12(R12), .in13(R13), .in14(R14), .in15(R15), .in16(R16),
    .in17(R17), .in18(R18), .in19(R19), .in20(R20), .in21(R21), .in22(R22), .in23(R23), .in24(R24),
    .in25(R25), .in26(R26), .in27(R27), .in28(R28), .in29(R29), .in30(R30), .in31(R31), .out(rdata1), .sel(rs));
  Register #(.width(32)) _17 (.D(wd), .en(EN17), .Q(R17), .clk(clk), .clr(clr));
  Register #(.width(32)) _18 (.D(wd), .en(EN18), .Q(R18), .clk(clk), .clr(clr));
  Register #(.width(32)) _19 (.D(wd), .en(EN19), .Q(R19), .clk(clk), .clr(clr));
  Register #(.width(32)) _20 (.D(wd), .en(EN20), .Q(R20), .clk(clk), .clr(clr));
  Register #(.width(32)) _21 (.D(wd), .en(EN21), .Q(R21), .clk(clk), .clr(clr));
  Register #(.width(32)) _22 (.D(wd), .en(EN22), .Q(R22), .clk(clk), .clr(clr));
  Register #(.width(32)) _23 (.D(wd), .en(EN23), .Q(R23), .clk(clk), .clr(clr));
  Register #(.width(32)) _24 (.D(wd), .en(EN24), .Q(R24), .clk(clk), .clr(clr));
  Multiplexer #(.select(5), .width(32), .disabled(0), .enable("false")) multiplexer_2 (
    .in0({32{1'b0}}), .in1(R01), .in2(R02), .in3(R03), .in4(R04), .in5(R05), .in6(R06), .in7(R07), .in8(R08),
    .in9(R09), .in10(R10), .in11(R11), .in12(R12), .in13(R13), .in14(R14), .in15(R15), .in16(R16),
    .in17(R17), .in18(R18), .in19(R19), .in20(R20), .in21(R21), .in22(R22), .in23(R23), .in24(R24),
    .in25(R25), .in26(R26), .in27(R27), .in28(R28), .in29(R29), .in30(R30), .in31(R31), .out(rdata2), .sel(rt));
  Register #(.width(32)) _25 (.D(wd), .en(EN25), .Q(R25), .clk(clk), .clr(clr));
  Register #(.width(32)) _26 (.D(wd), .en(EN26), .Q(R26), .clk(clk), .clr(clr));
  Register #(.width(32)) _27 (.D(wd), .en(EN27), .Q(R27), .clk(clk), .clr(clr));
  Register #(.width(32)) _28 (.D(wd), .en(EN28), .Q(R28), .clk(clk), .clr(clr));
  Register #(.width(32)) _29 (.D(wd), .en(EN29), .Q(R29), .clk(clk), .clr(clr));
  Register #(.width(32)) _30 (.D(wd), .en(EN30), .Q(R30), .clk(clk), .clr(clr));
  Register #(.width(32)) _31 (.D(wd), .en(EN31), .Q(R31), .clk(clk), .clr(clr));

  // Other names for the same wires on the sheet: RESET = clr
endmodule

module CTRL (
  input  [31:0] pc,
  input  [5:0] opcode,
  input  [4:0] rs,
  input  [4:0] rt,
  input  [4:0] rd,
  input  [4:0] shamt,
  input  [5:0] funct,
  input  [15:0] imm,
  input  [25:0] jmm,
  input  [31:0] rs_2,
  input  [31:0] rt_2,
  input  [31:0] memData,
  output memStore,
  output [31:0] memAddr,
  output [31:0] memStoreData,
  output regStore,
  output [4:0] regAddr,
  output [31:0] regStoreData,
  output pcStore,
  output [31:0] pcStoreData
);

  wire comparator_1_eq, comparator_2_eq, comparator_3_eq, comparator_4_eq, comparator_5_eq, comparator_6_eq,
       comparator_7_eq, comparator_8_eq, comparator_9_eq, comparator_10_eq, comparator_11_eq,
       comparator_12_eq, controlled_buffer_1_out, controlled_buffer_2_out, controlled_buffer_12_out;
  wire [31:0] adder_1_out, adder_2_out, adder_3_out, adder_4_out, adder_5_out, bit_extender_1_out,
       bit_extender_2_out, bit_extender_3_out, bit_extender_4_out, or_1_out, subtractor_1_out;

  Comparator #(.width(6)) comparator_1 (.a(opcode), .b({6{1'b0}}), .eq(comparator_1_eq));  // open: gt, lt
  Comparator #(.width(6)) comparator_2 (.a(opcode), .b({6{1'b0}}), .eq(comparator_2_eq));  // open: gt, lt
  Comparator #(.width(6)) comparator_3 (.a(opcode), .b(6'b001111), .eq(comparator_3_eq));  // open: gt, lt
  Comparator #(.width(6)) comparator_4 (.a(opcode), .b(6'b101011), .eq(comparator_4_eq));  // open: gt, lt
  assign bit_extender_1_out = {{16{imm[15]}}, imm};  // Bit_Extender bit_extender_1
  // Probe on pc
  // Probe on opcode
  // Probe on rs
  // Probe on rt
  // Probe on rd
  // Probe on shamt
  // Probe on funct
  // Probe on imm
  // Probe on jmm
  // Probe on rs_2
  // Probe on rt_2
  // Probe on memData
  Comparator #(.width(6)) comparator_5 (.a(funct), .b({6{1'b0}}), .eq(comparator_5_eq));  // open: gt, lt
  assign controlled_buffer_1_out = comparator_1_eq ? comparator_5_eq : 1'bz;  // Controlled_Buffer controlled_buffer_1
  assign controlled_buffer_2_out = comparator_2_eq ? comparator_6_eq : 1'bz;  // Controlled_Buffer controlled_buffer_2
  Comparator #(.width(6)) comparator_6 (.a(funct), .b(6'b100010), .eq(comparator_6_eq));  // open: gt, lt
  Subtractor #(.width(32)) subtractor_1 (.a(rs_2), .b(rt_2), .out(subtractor_1_out));  // open: bin, bout
  Adder #(.width(32)) adder_1 (.a(rs_2), .b(bit_extender_1_out), .out(adder_1_out));  // open: cin, cout
  Pull_Resistor pull_resistor_1 (.node(controlled_buffer_1_out));
  Pull_Resistor pull_resistor_2 (.node(controlled_buffer_2_out));
  Pull_Resistor pull_resistor_3 (.node(comparator_3_eq));
  Pull_Resistor pull_resistor_4 (.node(comparator_4_eq));
  // Probe on memStore
  // Probe on memAddr
  // Probe on memStoreData
  // Probe on regStore
  // Probe on regAddr
  // Probe on regStoreData
  // Probe on pcStore
  // Probe on pcStoreData
  assign regStoreData = controlled_buffer_2_out ? subtractor_1_out : 32'bz;  // Controlled_Buffer controlled_buffer_3
  assign regAddr = controlled_buffer_2_out ? rd : 5'bz;  // Controlled_Buffer controlled_buffer_4
  assign regStore = controlled_buffer_2_out ? 1'b1 : 1'bz;  // Controlled_Buffer controlled_buffer_5
  assign regStoreData = comparator_3_eq ? {imm, {16{1'b0}}} : 32'bz;  // Controlled_Buffer controlled_buffer_6
  assign regAddr = comparator_3_eq ? rt : 5'bz;  // Controlled_Buffer controlled_buffer_7
  assign regStore = comparator_3_eq ? 1'b1 : 1'bz;  // Controlled_Buffer controlled_buffer_8
  assign memStoreData = comparator_4_eq ? rt_2 : 32'bz;  // Controlled_Buffer controlled_buffer_9
  assign memAddr = comparator_4_eq ? adder_1_out : 32'bz;  // Controlled_Buffer controlled_buffer_10
  assign memStore = comparator_4_eq ? 1'b1 : 1'bz;  // Controlled_Buffer controlled_buffer_11
  Pull_Resistor pull_resistor_5 (.node(memStore));
  Pull_Resistor pull_resistor_6 (.node(regStore));
  Pull_Resistor pull_resistor_7 (.node(pcStore));
  Comparator #(.width(6)) comparator_7 (.a(opcode), .b({6{1'b0}}), .eq(comparator_7_eq));  // open: gt, lt
  Comparator #(.width(6)) comparator_8 (.a(opcode), .b(6'b001101), .eq(comparator_8_eq));  // open: gt, lt
  Comparator #(.width(6)) comparator_9 (.a(opcode), .b(6'b100011), .eq(comparator_9_eq));  // open: gt, lt
  Comparator #(.width(6)) comparator_10 (.a(opcode), .b(6'b000100), .eq(comparator_10_eq));  // open: gt, lt
  assign bit_extender_2_out = {{16{1'b0}}, imm};  // Bit_Extender bit_extender_2
  assign bit_extender_3_out = {{16{imm[15]}}, imm};  // Bit_Extender bit_extender_3
  assign bit_extender_4_out = {{14{imm[15]}}, {imm, 2'b00}};  // Bit_Extender bit_extender_4
  Adder #(.width(32)) adder_2 (.a(pc), .b(32'h4), .out(adder_2_out));  // open: cin, cout
  assign controlled_buffer_12_out = comparator_7_eq ? comparator_11_eq : 1'bz;  // Controlled_Buffer controlled_buffer_12
  Comparator #(.width(6)) comparator_11 (.a(funct), .b(6'b100000), .eq(comparator_11_eq));  // open: gt, lt
  Pull_Resistor pull_resistor_8 (.node(controlled_buffer_12_out));
  Adder #(.width(32)) adder_3 (.a(rs_2), .b(rt_2), .out(adder_3_out));  // open: cin, cout
  Pull_Resistor pull_resistor_9 (.node(comparator_8_eq));
  assign or_1_out = rs_2 | bit_extender_2_out;  // OR_Gate or_1, 32 bits wide
  Pull_Resistor pull_resistor_10 (.node(comparator_9_eq));
  Adder #(.width(32)) adder_4 (.a(rs_2), .b(bit_extender_3_out), .out(adder_4_out));  // open: cin, cout
  Pull_Resistor pull_resistor_11 (.node(comparator_10_eq));
  assign regStore = controlled_buffer_12_out ? 1'b1 : 1'bz;  // Controlled_Buffer controlled_buffer_13
  assign regStore = comparator_8_eq ? 1'b1 : 1'bz;  // Controlled_Buffer controlled_buffer_14
  assign memAddr = comparator_9_eq ? adder_4_out : 32'bz;  // Controlled_Buffer controlled_buffer_15
  Adder #(.width(32)) adder_5 (.a(bit_extender_4_out), .b(adder_2_out), .out(adder_5_out));  // open: cin, cout
  Comparator #(.width(32)) comparator_12 (.a(rs_2), .b(rt_2), .eq(comparator_12_eq));  // open: gt, lt
  assign pcStore = comparator_10_eq ? comparator_12_eq : 1'bz;  // Controlled_Buffer controlled_buffer_16
  assign regStoreData = controlled_buffer_12_out ? adder_3_out : 32'bz;  // Controlled_Buffer controlled_buffer_17
  assign regAddr = controlled_buffer_12_out ? rd : 5'bz;  // Controlled_Buffer controlled_buffer_18
  assign regStoreData = comparator_8_eq ? or_1_out : 32'bz;  // Controlled_Buffer controlled_buffer_19
  assign regAddr = comparator_8_eq ? rt : 5'bz;  // Controlled_Buffer controlled_buffer_20
  assign regStoreData = comparator_9_eq ? memData : 32'bz;  // Controlled_Buffer controlled_buffer_21
  assign regAddr = comparator_9_eq ? rt : 5'bz;  // Controlled_Buffer controlled_buffer_22
  assign regStore = comparator_9_eq ? 1'b1 : 1'bz;  // Controlled_Buffer controlled_buffer_23
  assign pcStoreData = comparator_10_eq ? adder_5_out : 32'bz;  // Controlled_Buffer controlled_buffer_24

  // Other names for the same wires on the sheet: rs_t[31:0] = rs_2; rt_t[31:0] = rt_2

  // Notes on the sheet:
  //   NOP: TEMPLATE
  //   SUB: rd <- rs - rt
  //   LUI: rt <- imm << 16
  //   SW: M[$rs + imm] <- rt
  //   ADD: rd <- rs + rt
  //   ORI: rt <- rs | imm
  //   LW: rt <- M[$rs + imm]
  //   BEQ: pc <- pc + 4 + SignedExt(imm * 4)
endmodule

module DM (
  input  memStore,
  input  [31:0] memAddr,
  input  [31:0] memStoreData,
  input  clk,
  input  clr,
  output [31:0] memData
);

  RAM #(.addrWidth(24), .dataWidth(32), .bus("separate")) ram_1 (
    .addr(memAddr[25:2]), .din(memStoreData), .data(memData), .str(memStore), .clk(clk), .ld(1'b1), .clr(clr));  // open: sel
endmodule
